# Fritzing sketch pythonPlayShutdownWiring (saved by Fritzing 0.9.3b)

parts:
  Raspberry_Pi_1 = Raspberry Pi 3 [part_number=RPI-3-V1.2]
  Shutdown_LED = LED - 5mm [color="Red (633nm)" package="5 mm [THT]"]
  Shutdown_Button = Pushbutton [package="[THT]"]
  R1 = Resistor [tolerance=±5% resistance=330 package=THT]
  Play_Button = Pushbutton [package="[THT]"]

nets:
  N1: Raspberry_Pi_1.GND, Shutdown_Button.Pin_3, Shutdown_Button.Pin_4, R1.Pin_1, Play_Button.Pin_1, Play_Button.Pin_2
  N2: Raspberry_Pi_1.GIPO21, Shutdown_Button.Pin_1, Shutdown_Button.Pin_2
  N3: Raspberry_Pi_1.GIPO16, Shutdown_LED.anode
  N4: Raspberry_Pi_1.GIPO14, Play_Button.Pin_3
  N5: Shutdown_LED.cathode, R1.Pin_0
